# Fritzing sketch Main (saved by Fritzing 0.9.3b)
breadboards: 1

parts:
  S1 = Pushbutton [package="[SMD]"]
  S2 = Pushbutton [package="[SMD]"]
  S3 = Pushbutton [package="[SMD]"]
  S4 = Pushbutton [package="[SMD]"]
  U1 = 4RelayModule
  SM1 = 28BYJ-48 Stepper Motor [part_number=28BYJ-48]
  Driver1 = 28BYJ-48 Driver Module [part_number=ULN2003 package=THT]
  Raspberry_Pi_1 = Raspberry Pi 4 [part_number=RPI-4-b]
  VCC1 = 4 x AAA Battery Mount
  Nokia_5110_LCD_Module1 = Nokia 5110 LCD

nets:
  N1: S1.Pin_1, S1.Pin_2, Raspberry_Pi_1.GPIO21
  GND: S1.Pin_3, S1.Pin_4, S2.Pin_3, S2.Pin_4, S3.Pin_3, S3.Pin_4, S4.Pin_3, S4.Pin_4, U1.GND, Driver1.GND, Raspberry_Pi_1.GND, VCC1.-, Nokia_5110_LCD_Module1.LED, Nokia_5110_LCD_Module1.LED_(out)
  N2: S2.Pin_1, S2.Pin_2, Raspberry_Pi_1.GPIO20
  N3: S3.Pin_1, S3.Pin_2, Raspberry_Pi_1.GPIO16
  N4: S4.Pin_1, S4.Pin_2, Raspberry_Pi_1.GPIO12
  N5: U1.IN2, Raspberry_Pi_1.GPIO17
  N6: U1.IN1, Raspberry_Pi_1.GPIO4
  VCC: U1.VCC, Raspberry_Pi_1.5V
  N7: SM1.blue-pin, Driver1.blue-pin
  N8: SM1.pink-pin, Driver1.pink-pin
  N9: SM1.yellow-pin, Driver1.yellow-pin
  N10: SM1.orange-pin, Driver1.orange-pin
  N11: SM1.red-pin, Driver1.red-pin
  N12: Driver1.IN1, Raspberry_Pi_1.GPIO26
  N13: Driver1.IN2, Raspberry_Pi_1.GPIO19
  N14: Driver1.IN3, Raspberry_Pi_1.GPIO13
  N15: Driver1.IN4, Raspberry_Pi_1.GPIO6
  N16: Driver1.Vmotor, VCC1.+
  N17: Raspberry_Pi_1.3v3, Nokia_5110_LCD_Module1.DN(MOSI), Nokia_5110_LCD_Module1.SCLK, Nokia_5110_LCD_Module1.SCLK_(out)
  N18: Raspberry_Pi_1.GPIO27, Nokia_5110_LCD_Module1.VCC, Nokia_5110_LCD_Module1.VCC_(out)
  N19: Raspberry_Pi_1.GPIO22, Nokia_5110_LCD_Module1.SCE, Nokia_5110_LCD_Module1.SCE_(out)
  N20: Raspberry_Pi_1.GPIO10, Nokia_5110_LCD_Module1.RST, Nokia_5110_LCD_Module1.RST_(out)
  N21: Raspberry_Pi_1.GPIO11, Nokia_5110_LCD_Module1.D/C, Nokia_5110_LCD_Module1.D/C_(out)
  N22: Raspberry_Pi_1.GPIO8, Nokia_5110_LCD_Module1.GND, Nokia_5110_LCD_Module1.GND_(out)

custom parts:
  4RelayModule: 4 relay arduino module SONGLE SRD05VDC-SL-C
  28BYJ-48 Stepper Motor: Unipolar Stepper Motor 28BYJ-48 Top coil - pink & orange Bottom coil - blue & yellow Common rail - red Connector pins: blue - pink - yellow - orange - red
  28BYJ-48 Driver Module: High-power ULN2003 Stepper Motor Driver Board Test Module For Arduino AVR SMD
  Raspberry Pi 4: The RPi4, a faster version of the awesome Raspberry Pi 2 B ARM Board with 40 pin gpio. Ready for special Raspberry Pi B+ and RPi2 Hat (Hardware attached (on) top)
  Nokia 5110 LCD: Nokia 5110 Graphic 84*48 LCD module such as the Sparkfun LCD-10168 or the clones from Ebay. There is example code for the Arduino available from the Sparkfun site in https://learn.sparkfun.com/tutorials/graphic-lcd-hookup-guide This is a 3.3V device, if you are running it from a 5V micro you need a 5V tolorant level translator such as the 74ahc367 to protect the signal imputs. Rafa G. did a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
